// Logisim project logisim.circ as structural Verilog: 1 circuit, main circuit main
module main (
  input  S1,
  input  S2,
  input  S3,
  output F
);

  wire AND3_1_out, AND3_2_out, AND3_3_out, AND3_4_out, INV_1_out, INV_2_out, INV_3_out;

  not INV_1 (INV_1_out, S1);
  not INV_2 (INV_2_out, S2);
  not INV_3 (INV_3_out, S3);
  and AND3_1 (AND3_1_out, S1, INV_2_out, INV_3_out);
  and AND3_2 (AND3_2_out, INV_1_out, S2, INV_3_out);
  and AND3_3 (AND3_3_out, INV_1_out, INV_2_out, S3);
  and AND3_4 (AND3_4_out, S2, S3, S1);
  or OR4_1 (F, AND3_1_out, AND3_2_out, AND3_3_out, AND3_4_out);
endmodule
