// Logisim project Cou.circ as structural Verilog: 2 circuits, main circuit FD
module FD (
  input  D,
  input  clk,
  output Q,
  output Qn
);
endmodule

module Counter4b (
  input  clk,
  output Qa,
  output Qb,
  output Qc,
  output Qd,
  output Rc
);

  wire FD1_qn, FD2_qn, FD3_qn, FD4_qn, nor_1_out, nor_2_out, not_1_out, not_2_out, not_3_out, not_4_out,
       xor_1_out, xor_2_out, xor_3_out;

  not not_1 (not_1_out, FD1_qn);
  nor nor_1 (nor_1_out, FD1_qn, FD2_qn);
  nor nor_2 (nor_2_out, FD1_qn, FD3_qn, FD2_qn);
  xor xor_1 (xor_1_out, not_1_out, FD2_qn);
  xor xor_2 (xor_2_out, nor_1_out, FD3_qn);
  xor xor_3 (xor_3_out, nor_2_out, FD4_qn);
  not not_2 (not_2_out, xor_1_out);
  not not_3 (not_3_out, xor_2_out);
  not not_4 (not_4_out, xor_3_out);
  FD FD1 (.D(FD1_qn), .clk(clk), .Q(Qa), .Qn(FD1_qn));
  FD FD2 (.D(not_2_out), .clk(clk), .Q(Qb), .Qn(FD2_qn));
  FD FD3 (.D(not_3_out), .clk(clk), .Q(Qc), .Qn(FD3_qn));
  FD FD4 (.D(not_4_out), .clk(clk), .Q(Qd), .Qn(FD4_qn));
  nor nor_3 (Rc, FD4_qn, FD3_qn, FD2_qn, FD1_qn);
endmodule
