// Logisim project D.circ as structural Verilog: 3 circuits, main circuit D_74LS138
module D_74LS138 (
  input  A,
  input  B,
  input  C,
  input  G,
  input  G2A,
  input  G2B,
  output [7:0] Y
);

  wire AND2_1_out, AND2_2_out, AND2_3_out, AND2_4_out, INV_A_out, INV_B_out, INV_C_out, INV_G_out, NOR3_1_out;

  not INV_G (INV_G_out, G);
  not INV_A (INV_A_out, A);
  not INV_B (INV_B_out, B);
  not INV_C (INV_C_out, C);
  nor NOR3_1 (NOR3_1_out, INV_G_out, G2A, G2B);
  and AND2_1 (AND2_1_out, INV_A_out, INV_B_out);
  and AND2_2 (AND2_2_out, A, INV_B_out);
  and AND2_3 (AND2_3_out, INV_A_out, B);
  and AND2_4 (AND2_4_out, A, B);
  nand NAND3_1 (Y[0], AND2_1_out, NOR3_1_out, INV_C_out);
  nand NAND3_2 (Y[1], AND2_2_out, NOR3_1_out, INV_C_out);
  nand NAND3_3 (Y[2], AND2_3_out, NOR3_1_out, INV_C_out);
  nand NAND3_4 (Y[3], AND2_4_out, NOR3_1_out, INV_C_out);
  nand NAND3_5 (Y[4], AND2_1_out, NOR3_1_out, C);
  nand NAND3_6 (Y[5], AND2_2_out, NOR3_1_out, C);
  nand NAND3_7 (Y[6], AND2_3_out, NOR3_1_out, C);
  nand NAND3_8 (Y[7], AND2_4_out, NOR3_1_out, C);
endmodule

module LampCtrl (
  input  S3,
  input  S2,
  input  S1,
  output F
);

  wire [7:0] D_74LS138_1_y;

  D_74LS138 D_74LS138_1 (.A(S3), .B(S2), .C(S1), .G(1'b1), .G2A(1'b0), .G2B(1'b0), .Y(D_74LS138_1_y));
  nand NAND4_1 (F, D_74LS138_1_y[1], D_74LS138_1_y[2], D_74LS138_1_y[4], D_74LS138_1_y[7]);
endmodule

module D_74LS138_Test (
  input  [5:0] SW,
  output [7:0] LED
);

  D_74LS138 D_74LS138_1 (.A(SW[2]), .B(SW[1]), .C(SW[0]), .G(SW[5]), .G2A(SW[3]), .G2B(SW[4]), .Y(LED));
endmodule
